# Fritzing sketch 5.1 (saved by Fritzing 0.9.3b)
breadboards: 1

parts:
  LED1 = LEDs [package=led10mm]
  Part3 = Lilypad Battery Connect
  PIR1 = PIR sensor
  Part4 = Arduino Uno (Rev3) - ICSP
  U1 = 2-Channel 5v Relay Shield [package=relay-2ch5v10a]

nets:
  N1: LED1.A, U1.K1-In
  N2: LED1.C, Part3.+
  N3: Part3.-, U1.K1-On
  VDD: PIR1.VDD, Part4.5V, U1.VCC
  N4: PIR1.SIG, Part4.D8
  GND: PIR1.GND, Part4.GND, U1.GND
  N5: Part4.D7, U1.IN1

custom parts:
  LEDs: LEDs Standard schematic elements and footprints for 5mm, 3mm, 1206, and 0603 sized LEDs. 5mm - Spark Fun Electronics SKU : COM-00529 (and others)
  2-Channel 5v Relay Shield: 2 Channel 5v Relay Shield w. 2x SPD-06VDC-SD-C
