# Fritzing sketch HC-05 Bluetooth Module (saved by Fritzing 0.9.3b)
breadboards: 1

parts:
  Part1 = Bluetooth HC-05 Macho
  Part3 = Arduino Uno (Rev3) - ICSP
  LED1 = smd LED [color="Red (633nm)" package="0603 [SMD]"]  # not connected
  R1 = Resistor [tolerance=±5% resistance=220 package="0603 [SMD]"]

nets:
  N1: Part1.TXD, Part3.D0/RX
  N2: Part1.RXD, Part3.D1/TX
  VCC: Part1.VCC, Part3.5V
  GND: Part1.GND, Part3.GND
  N3: Part3.D13/SCK, R1.Pin_0
