# Fritzing sketch Ultrasonic_Sensor_HC-SR04_and_LCD_Display_With_I2C (saved by Fritzing 0.9.3b)
breadboards: 1

parts:
  Part1 = LCD1602-I2C
  Part2 = Arduino Uno (Rev3) - ICSP
  HC-SR04_Sensor_1 = HC-SR04 Ultrasonic Distance Sensor

nets:
  GND: Part1.GND, Part2.GND, HC-SR04_Sensor_1.GND
  VCC: Part1.VCC, Part2.5V, HC-SR04_Sensor_1.VCC
  N1: Part1.SDA, Part2.A4/SDA
  N2: Part1.SCL, Part2.A5/SCL
  N3: Part2.D9_PWM, HC-SR04_Sensor_1.TRIG
  N4: Part2.D10_PWM/SS, HC-SR04_Sensor_1.ECHO

custom parts:
  LCD1602-I2C: A standard character display, usually with 2x16 characters. Comes in many colors with LCM1602 IIC attached.
