# Fritzing sketch motor_lcd (saved by Fritzing 0.9.3b)
breadboards: 1

parts:
  U1 = 2-Channel 5v Relay Shield [package=relay-2ch5v10a]
  S1 = Pushbutton [package="[THT]"]
  S2 = Pushbutton [package="[THT]"]
  S3 = Pushbutton [package="[THT]"]
  R1 = Resistor [tolerance=±5% resistance=1k package=THT]
  R2 = Resistor [tolerance=±5% resistance=1k package=THT]
  R3 = Resistor [tolerance=±5% resistance=1k package=THT]
  VCC1 = Battery block 9V
  Part1 = Arduino Uno (Rev3) - ICSP
  M1 = DC Motor
  Part2 = LCD1602-I2C

nets:
  VCC: U1.VCC, S1.Pin_3, S1.Pin_4, S2.Pin_3, S2.Pin_4, S3.Pin_3, S3.Pin_4, Part1.5V, Part2.VCC
  GND: U1.GND, R1.Pin_0, R2.Pin_0, R3.Pin_0, Part1.GND, Part2.GND
  N1: U1.IN1, Part1.D12/MISO
  N2: U1.IN2, Part1.D13/SCK
  N3: U1.K1-In, M1.pin_1
  N4: U1.K1-Off, U1.K2-Off, VCC1.-
  N5: U1.K1-On, U1.K2-On, VCC1.+
  N6: U1.K2-In, M1.pin_2
  N7: S1.Pin_1, S1.Pin_2, R1.Pin_1, Part1.D4
  N8: S2.Pin_1, S2.Pin_2, R2.Pin_1, Part1.D3_PWM
  N9: S3.Pin_1, S3.Pin_2, R3.Pin_1, Part1.D2
  N10: Part1.A4/SDA, Part2.SDA
  N11: Part1.A5/SCL, Part2.SCL

notes:
  +
  -
  Forward
  Reverse
  Stop

custom parts:
  2-Channel 5v Relay Shield: 2 Channel 5v Relay Shield w. 2x SPD-06VDC-SD-C
  LCD1602-I2C: A standard character display, usually with 2x16 characters. Comes in many colors with LCM1602 IIC attached.
