# Fritzing sketch sensor (saved by Fritzing 0.9.3b)
breadboards: 1

parts:
  KY-1 = Keyes Relay [package=THT]
  Part2 = Lilypad Battery Connect
  PIR1 = PIR sensor  # not connected
  Part3 = Arduino Uno (Rev3) - ICSP  # not connected
  LED2 = LEDs [package=led10mm]

nets:
  N1: KY-1.C, Part2.+
  N2: KY-1.NO, LED2.C
  N3: Part2.-, LED2.A

notes:
  IN
  GND
  VCC
  240V AC power supply

custom parts:
  Keyes Relay: The Keyes 5V relay module is suitable for SCM development, home appliance control. It uses a 5V~12V TIL control signal which can control DC / AC signal.
  LEDs: LEDs Standard schematic elements and footprints for 5mm, 3mm, 1206, and 0603 sized LEDs. 5mm - Spark Fun Electronics SKU : COM-00529 (and others)
